# Fritzing sketch SPI_Fritzing (saved by Fritzing 0.9.3b)
breadboards: 1

parts:
  IC1 = MICROCONTROLLER [package=dil28-3]
  Power_plug1 = Power plug
  IC2 = MICROCONTROLLER [package=dil28-3]
  LED1 = LED - 5mm [color="Red (633nm)" package="5 mm [THT]"]
  R1 = Resistor [tolerance=±5% resistance=220 package=THT]

nets:
  VCC: IC1.VCC, Power_plug1.VCC, IC2.VCC
  GND: IC1.GND, Power_plug1.GND, IC2.GND, LED1.cathode
  N1: IC1.PB1(OC1A), IC2.PB1(OC1A)
  N2: IC1.PB2(SS_OC1B), IC2.PB2(SS_OC1B)
  N3: IC1.PB3(MOSI_OC2), IC2.PB3(MOSI_OC2)
  N4: IC1.PB4(MISO), IC2.PB4(MISO)
  N5: IC2.PC5(ADC5_SCL), R1.Pin_0
  N6: LED1.anode, R1.Pin_1
