# Fritzing sketch Fading_LED_Fritzing (saved by Fritzing 0.9.3b)
breadboards: 1

parts:
  IC1 = MICROCONTROLLER [package=dil28-3]
  R1 = Resistor [tolerance=±5% resistance=220 package=THT]
  LED1 = LED - 5mm [color="Red (633nm)" package="5 mm [THT]"]
  R2 = Rotary Potentiometer (Small) [maximum_resistance=100kΩ package=THT]
  Power_plug1 = Power plug

nets:
  VCC: IC1.VCC, Power_plug1.VCC
  GND: IC1.GND, Power_plug1.GND
  N1: IC1.PB1(OC1A), R1.Pin_0
  N2: IC1.AVCC, R2.leg2
  N3: IC1.AGND, R2.leg1
  N4: IC1.PC0(ADC0), R2.wiper
  N5: R1.Pin_1, LED1.anode
